# Fritzing sketch minimal-breadboard-v1 (saved by Fritzing 0.9.3b)
breadboards: 1

parts:
  U1 = ESP8266 WiFi Module [part_number=ESP8266]
  R1 = Resistor [tolerance=±5% resistance=1k package=THT]
  R2 = Resistor [tolerance=±5% resistance=1k package=THT]
  R3 = Resistor [tolerance=±5% resistance=1k package=THT]
  U3 = V_REG_LD1117VXX [package=78xxl]
  C1 = Electrolytic Capacitor [capacitance=10µF package="100 mil [THT, electrolytic]"]
  C2 = Electrolytic Capacitor [capacitance=100µF package="100 mil [THT, electrolytic]"]
  DHT1 = DHT22 Humidity and Temperature Sensor
  Part1 = Adafruit Micro USB Breakout [part_number="Adafruit #1833"]
  R4 = Resistor [tolerance=±5% resistance=3.3k package=THT]

nets:
  N1: U1.IO2, DHT1.DATA, R4.Pin_0
  N2: U1.3.3V#11, R2.Pin_1, R3.Pin_1, U3.OUT, C1.+, DHT1.VDD, R4.Pin_1
  GND: U1.GND#12, R1.Pin_1, U3.GND, C1.-, C2.-, DHT1.GND, Part1.GND
  N3: U1.RST, R3.Pin_0
  N4: U1.CHIP_EN, R2.Pin_0
  N5: U1.IO15, R1.Pin_0
  N6: U3.IN, C2.+, Part1.VBUS

custom parts:
  Adafruit Micro USB Breakout: Simple but effective - this breakout board has a USB Micro-B connector, with all 5 pins broken out. Great for pairing with a microcontroller with USB support, or adding USB 5V power to a project. We use a micro-AB connector with through-hole shielding pads for an excellent strong connection - it won't rip off by accident! Comes with one fully assembled and tested micro B breakout PCB and a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
